# Fritzing sketch fsm_alarm (saved by Fritzing 0.9.3b)
breadboards: 1

parts:
  J2 = STM32 Nucleo boards
  Part1 = HC-SR501 Body Sensor Module

nets:
  N1: J2.D6_PWM, Part1.OUT
  5V: J2.5V, Part1.VCC
  GND: J2.GND, Part1.GND

custom parts:
  HC-SR501 Body Sensor Module: Pyroelectric Infrared PIR Motion Sensor Detector Module
